// Logisim project project.circ as structural Verilog
module main (
  output [31:0] INSTRUCTION,
  output [7:0] out_2
);

  wire clock_1_out, RESET_out;

  Clock clock_1 (.out(clock_1_out));
  Button RESET (.out(RESET_out));
  ROM #(.dataWidth(32)) rom_1 (.addr(out_2), .data(INSTRUCTION));
  PC pc_1 (.clk(clock_1_out), .reset(RESET_out), .out_3(out_2));

  // Notes on the sheet:
  //   contents of rom_1 (hex, n*v repeats v):
  //   100000 1000
endmodule

module PC (
  input  clk,
  input  reset,
  output [7:0] out_3
);

  wire [31:0] adder_1_out, register_1_q;

  Adder #(.width(32)) adder_1 (
    .a(32'h4), .b({register_1_q[31:10], out_3, register_1_q[1:0]}), .out(adder_1_out));  // open: cin, cout
  Register #(.width(32)) register_1 (
    .D(adder_1_out), .clk(clk), .Q({register_1_q[31:10], out_3, register_1_q[1:0]}), .clr(reset));  // open: en
endmodule

module BancoDeRegistradores (
  input  [2:0] in_1,
  input  clk,
  input  [2:0] R1,
  input  [3:0] RW1,
  input  [7:0] RD1,
  input  [7:0] WR,
  input  [3:0] RW2,
  input  [7:0] RD2,
  input  [2:0] R2
);

  wire [7:0] demultiplexer_1_out0, demultiplexer_1_out1, demultiplexer_1_out4, demultiplexer_1_out7, REG0_q,
       REG1_q, REG3_q, REG4_q, REG6_q, REG7_q, undriven, undriven_2;

  Register REG0 (.D(demultiplexer_1_out0), .Q(REG0_q));  // open: en, clk, clr
  Register REG1 (.D(demultiplexer_1_out1), .Q(REG1_q));  // open: en, clk, clr
  Register REG2 (.D(undriven), .Q(REG0_q));  // open: en, clk, clr
  Register REG3 (.D(undriven_2), .Q(REG3_q));  // open: en, clk, clr
  Multiplexer #(.select(3), .width(8)) multiplexer_1 (
    .in0(REG0_q), .in1(REG1_q), .in2(REG0_q), .in4(REG4_q), .in5(REG0_q), .in6(REG6_q), .in7(REG7_q),
    .out(RD1), .sel(R1));  // open: in3
  Register REG7 (.D(demultiplexer_1_out7), .Q(REG7_q));  // open: en, clk, clr
  Register REG6 (.Q(REG6_q));  // open: D, en, clk, clr
  Register REG5 (.Q(REG0_q));  // open: D, en, clk, clr
  Register REG4 (.D(demultiplexer_1_out4), .Q(REG4_q));  // open: en, clk, clr
  Demultiplexer #(.select(3), .width(8)) demultiplexer_1 (
    .out0(demultiplexer_1_out0), .out1(demultiplexer_1_out1), .out4(demultiplexer_1_out4),
    .out7(demultiplexer_1_out7), .in(WR));  // open: out2, out3, out5, out6, sel
  Multiplexer #(.select(3), .width(8)) multiplexer_2 (
    .in0(REG0_q), .in1(REG1_q), .in2(REG0_q), .in3(REG3_q), .in4(REG4_q), .in5(REG0_q), .in6(REG6_q),
    .in7(REG7_q), .out(RD2));  // open: sel
endmodule
